# Fritzing sketch Pinout_Raspberry_Pi (saved by Fritzing 0.9.6b)

parts:
  Raspberry_Pi_1 = Raspberry Pi 3 [part_number=RPI-3-V1.2]
  Display = female pin header, 2 pins [form="♀ (female)"]
  Level_Converter = Logic Level Converter

nets:
  N1: Raspberry_Pi_1.3v3, Level_Converter.LV
  GND: Raspberry_Pi_1.GND, Display.pin2, Level_Converter.GND
  N2: Raspberry_Pi_1.GPIO15, Level_Converter.RX2_LV
  N3: Raspberry_Pi_1.GPIO14, Level_Converter.TX2_LV
  N4: Raspberry_Pi_1.5V, Display.pin1

notes:
  Display
  Coffee Maker
